# Fritzing sketch led_cloud (saved by Fritzing 0.9.3b)
circuit board: 6.2559cm x 4.12673cm
breadboards: 1

parts:
  TRINKET_3V = mystery part, 10 pins [chip_label="Trinket 3V"]
  BLUE = Basic FET P-Channel [package="TO220 [THT]"]
  GREEN = Basic FET P-Channel [package="TO220 [THT]"]
  RED = Basic FET P-Channel [package="TO220 [THT]"]
  RGB_LED = RGB LED - (4 legs) [package="5 mm [THT]"]

nets:
  N1: TRINKET_3V.pin2, BLUE.source, GREEN.source, RED.source, RGB_LED.common_anode
  N2: TRINKET_3V.pin3, RED.gate, RGB_LED.red_cathode
  N3: TRINKET_3V.pin4, GREEN.gate, RGB_LED.green_cathode
  N4: TRINKET_3V.pin7, BLUE.gate, RGB_LED.blue_cathode
